# Fritzing sketch A Device for Tracing [Schematics] (saved by Fritzing 0.9.3b)
circuit board: 9cm x 7cm
breadboards: 1

parts:
  bat_OUT = Header 2 [package=jst-2-pth-ns]
  bat_IN = Header 2 [package=jst-2-pth-ns]
  power_in_9v = Header 2 [package=jst-2-pth-ns]
  6_8k = Resistor [tolerance=±5% resistance=220 package=THT]
  led_carga = LED - 5mm [color="Red (633nm)" package="5 mm [THT]"]
  diodo_4007 = DIODE-ZENER [package=diode-zener]
  switch = Header 2 [package=jst-2-pth-ns]
  led_out = Header 2 [package=jst-2-pth-ns]

nets:
  N1: bat_OUT.1, led_out.1
  N2: bat_IN.1, power_in_9v.1, led_carga.cathode
  N3: bat_IN.2, diodo_4007.C
  N4: power_in_9v.2, 6_8k.Pin_1, diodo_4007.A
  N5: 6_8k.Pin_0, led_carga.anode
  N6: switch.2, led_out.2

notes:
  5W22RJ
  2 baterias 18650
  3.7v / 5000mah
  2S protection board
  h-orizontal.org
  diseño original: julián bejarano
  caja de trazo
